// Logisim project RV32I.circ as structural Verilog: 8 circuits, main circuit rv32i
module reg_file (
  input  [31:0] in_1,
  input  Wen,
  input  [4:0] RS1,
  input  [4:0] RD,
  input  [4:0] RS2,
  input  in_6,
  input  in_7,
  output [31:0] out_8,
  output [31:0] out_9
);

  wire decoder_1_out0, decoder_1_out1, decoder_1_out2, decoder_1_out3, decoder_1_out4, decoder_1_out5,
       decoder_1_out6, decoder_1_out7, decoder_1_out8, decoder_1_out9, decoder_1_out10, decoder_1_out11,
       decoder_1_out12, decoder_1_out13, decoder_1_out14, decoder_1_out15, decoder_1_out16, decoder_1_out17,
       decoder_1_out18, decoder_1_out19, decoder_1_out20, decoder_1_out21, decoder_1_out22, decoder_1_out23,
       decoder_1_out24, decoder_1_out25, decoder_1_out26, decoder_1_out27, decoder_1_out28, decoder_1_out29,
       decoder_1_out30, decoder_1_out31;
  wire [31:0] multiplexer_1_out, register_1_q, register_2_q, register_3_q, register_4_q, register_5_q,
       register_6_q, register_7_q, register_8_q, register_9_q, register_10_q, register_11_q, register_12_q,
       register_13_q, register_14_q, register_15_q, register_16_q, register_17_q, register_18_q,
       register_19_q, register_20_q, register_21_q, register_22_q, register_23_q, register_24_q,
       register_25_q, register_26_q, register_27_q, register_28_q, register_29_q, register_30_q,
       register_31_q, register_32_q;

  Decoder #(.select(5)) decoder_1 (
    .out0(decoder_1_out0), .out1(decoder_1_out1), .out2(decoder_1_out2), .out3(decoder_1_out3),
    .out4(decoder_1_out4), .out5(decoder_1_out5), .out6(decoder_1_out6), .out7(decoder_1_out7),
    .out8(decoder_1_out8), .out9(decoder_1_out9), .out10(decoder_1_out10), .out11(decoder_1_out11),
    .out12(decoder_1_out12), .out13(decoder_1_out13), .out14(decoder_1_out14), .out15(decoder_1_out15),
    .out16(decoder_1_out16), .out17(decoder_1_out17), .out18(decoder_1_out18), .out19(decoder_1_out19),
    .out20(decoder_1_out20), .out21(decoder_1_out21), .out22(decoder_1_out22), .out23(decoder_1_out23),
    .out24(decoder_1_out24), .out25(decoder_1_out25), .out26(decoder_1_out26), .out27(decoder_1_out27),
    .out28(decoder_1_out28), .out29(decoder_1_out29), .out30(decoder_1_out30), .out31(decoder_1_out31),
    .sel(RD), .en(Wen));
  Multiplexer #(.width(32)) multiplexer_1 (.in1(in_1), .out(multiplexer_1_out), .sel(Wen));  // open: in0, en
  Register #(.width(32)) register_1 (.D({32{1'b0}}), .en(decoder_1_out0), .Q(register_1_q), .clk(in_6), .clr(in_7));
  Register #(.width(32)) register_2 (
    .D(multiplexer_1_out), .en(decoder_1_out1), .Q(register_2_q), .clk(in_6), .clr(in_7));
  Register #(.width(32)) register_3 (
    .D(multiplexer_1_out), .en(decoder_1_out2), .Q(register_3_q), .clk(in_6), .clr(in_7));
  Register #(.width(32)) register_4 (
    .D(multiplexer_1_out), .en(decoder_1_out3), .Q(register_4_q), .clk(in_6), .clr(in_7));
  Register #(.width(32)) register_5 (
    .D(multiplexer_1_out), .en(decoder_1_out4), .Q(register_5_q), .clk(in_6), .clr(in_7));
  Register #(.width(32)) register_6 (
    .D(multiplexer_1_out), .en(decoder_1_out5), .Q(register_6_q), .clk(in_6), .clr(in_7));
  Register #(.width(32)) register_7 (
    .D(multiplexer_1_out), .en(decoder_1_out6), .Q(register_7_q), .clk(in_6), .clr(in_7));
  Register #(.width(32)) register_8 (
    .D(multiplexer_1_out), .en(decoder_1_out7), .Q(register_8_q), .clk(in_6), .clr(in_7));
  Register #(.width(32)) register_9 (
    .D(multiplexer_1_out), .en(decoder_1_out8), .Q(register_9_q), .clk(in_6), .clr(in_7));
  Register #(.width(32)) register_10 (
    .D(multiplexer_1_out), .en(decoder_1_out9), .Q(register_10_q), .clk(in_6), .clr(in_7));
  Register #(.width(32)) register_11 (
    .D(multiplexer_1_out), .en(decoder_1_out10), .Q(register_11_q), .clk(in_6), .clr(in_7));
  Register #(.width(32)) register_12 (
    .D(multiplexer_1_out), .en(decoder_1_out11), .Q(register_12_q), .clk(in_6), .clr(in_7));
  Register #(.width(32)) register_13 (
    .D(multiplexer_1_out), .en(decoder_1_out12), .Q(register_13_q), .clk(in_6), .clr(in_7));
  Register #(.width(32)) register_14 (
    .D(multiplexer_1_out), .en(decoder_1_out13), .Q(register_14_q), .clk(in_6), .clr(in_7));
  Register #(.width(32)) register_15 (
    .D(multiplexer_1_out), .en(decoder_1_out14), .Q(register_15_q), .clk(in_6), .clr(in_7));
  Register #(.width(32)) register_16 (
    .D(multiplexer_1_out), .en(decoder_1_out15), .Q(register_16_q), .clk(in_6), .clr(in_7));
  Register #(.width(32)) register_17 (
    .D(multiplexer_1_out), .en(decoder_1_out16), .Q(register_17_q), .clk(in_6), .clr(in_7));
  Register #(.width(32)) register_18 (
    .D(multiplexer_1_out), .en(decoder_1_out17), .Q(register_18_q), .clk(in_6), .clr(in_7));
  Register #(.width(32)) register_19 (
    .D(multiplexer_1_out), .en(decoder_1_out18), .Q(register_19_q), .clk(in_6), .clr(in_7));
  Register #(.width(32)) register_20 (
    .D(multiplexer_1_out), .en(decoder_1_out19), .Q(register_20_q), .clk(in_6), .clr(in_7));
  Register #(.width(32)) register_21 (
    .D(multiplexer_1_out), .en(decoder_1_out20), .Q(register_21_q), .clk(in_6), .clr(in_7));
  Register #(.width(32)) register_22 (
    .D(multiplexer_1_out), .en(decoder_1_out21), .Q(register_22_q), .clk(in_6), .clr(in_7));
  Register #(.width(32)) register_23 (
    .D(multiplexer_1_out), .en(decoder_1_out22), .Q(register_23_q), .clk(in_6), .clr(in_7));
  Register #(.width(32)) register_24 (
    .D(multiplexer_1_out), .en(decoder_1_out23), .Q(register_24_q), .clk(in_6), .clr(in_7));
  Register #(.width(32)) register_25 (
    .D(multiplexer_1_out), .en(decoder_1_out24), .Q(register_25_q), .clk(in_6), .clr(in_7));
  Register #(.width(32)) register_26 (
    .D(multiplexer_1_out), .en(decoder_1_out25), .Q(register_26_q), .clk(in_6), .clr(in_7));
  Register #(.width(32)) register_27 (
    .D(multiplexer_1_out), .en(decoder_1_out26), .Q(register_27_q), .clk(in_6), .clr(in_7));
  Register #(.width(32)) register_28 (
    .D(multiplexer_1_out), .en(decoder_1_out27), .Q(register_28_q), .clk(in_6), .clr(in_7));
  Register #(.width(32)) register_29 (
    .D(multiplexer_1_out), .en(decoder_1_out28), .Q(register_29_q), .clk(in_6), .clr(in_7));
  Register #(.width(32)) register_30 (
    .D(multiplexer_1_out), .en(decoder_1_out29), .Q(register_30_q), .clk(in_6), .clr(in_7));
  Register #(.width(32)) register_31 (
    .D(multiplexer_1_out), .en(decoder_1_out30), .Q(register_31_q), .clk(in_6), .clr(in_7));
  Register #(.width(32)) register_32 (
    .D(multiplexer_1_out), .en(decoder_1_out31), .Q(register_32_q), .clk(in_6), .clr(in_7));
  Multiplexer #(.select(5), .width(32), .enable("false")) multiplexer_2 (
    .in0(register_1_q), .in1(register_2_q), .in2(register_3_q), .in3(register_4_q), .in4(register_5_q),
    .in5(register_6_q), .in6(register_7_q), .in7(register_8_q), .in8(register_9_q), .in9(register_10_q),
    .in10(register_11_q), .in11(register_12_q), .in12(register_13_q), .in13(register_14_q),
    .in14(register_15_q), .in15(register_16_q), .in16(register_17_q), .in17(register_18_q),
    .in18(register_19_q), .in19(register_20_q), .in20(register_21_q), .in21(register_22_q),
    .in22(register_23_q), .in23(register_24_q), .in24(register_25_q), .in25(register_26_q),
    .in26(register_27_q), .in27(register_28_q), .in28(register_29_q), .in29(register_30_q),
    .in30(register_31_q), .in31(register_32_q), .out(out_8), .sel(RS1));
  Multiplexer #(.select(5), .width(32), .enable("false")) multiplexer_3 (
    .in0(register_1_q), .in1(register_2_q), .in2(register_3_q), .in3(register_4_q), .in4(register_5_q),
    .in5(register_6_q), .in6(register_7_q), .in7(register_8_q), .in8(register_9_q), .in9(register_10_q),
    .in10(register_11_q), .in11(register_12_q), .in12(register_13_q), .in13(register_14_q),
    .in14(register_15_q), .in15(register_16_q), .in16(register_17_q), .in17(register_18_q),
    .in18(register_19_q), .in19(register_20_q), .in20(register_21_q), .in21(register_22_q),
    .in22(register_23_q), .in23(register_24_q), .in24(register_25_q), .in25(register_26_q),
    .in26(register_27_q), .in27(register_28_q), .in28(register_29_q), .in29(register_30_q),
    .in30(register_31_q), .in31(register_32_q), .out(out_9), .sel(RS2));
endmodule

module rv32i (
  input  in_1
);

  wire alu_1_branch, and_1_out, clock_1_out, control_1_out_2, control_1_out_3, control_1_out_4,
       control_1_out_5, control_1_out_6, control_1_out_7, control_1_out_9, control_1_out_10, or_2_out;
  wire [1:0] or_1_out;
  wire [4:0] alu_op_1_out_4, multiplexer_4_out, multiplexer_9_out;
  wire [19:0] PC_q_2;
  wire [31:0] adder_1_out, alu_1_out_4, bitextender_1_out_3, bitextender_1_out_6, bitextender_1_s_type,
       bitextender_1_u_type, bitextender_1_uj_type, multiplexer_1_out, multiplexer_2_out, multiplexer_3_out,
       multiplexer_5_out, multiplexer_6_out, multiplexer_7_out, multiplexer_8_out, multiplexer_10_out,
       multiplexer_11_out, PC_q, ram_1_data, reg_file_1_out_8, reg_file_1_out_9, rom_1_data;

  Multiplexer #(.width(32), .enable("false")) multiplexer_1 (
    .in0(adder_1_out), .in1(bitextender_1_out_6), .out(multiplexer_1_out), .sel(and_1_out));
  Multiplexer #(.width(32), .enable("false")) multiplexer_2 (
    .in0(multiplexer_1_out), .in1(bitextender_1_uj_type), .out(multiplexer_2_out), .sel(control_1_out_10));
  Multiplexer #(.width(32), .enable("false")) multiplexer_3 (
    .in0(multiplexer_2_out), .in1(multiplexer_11_out), .out(multiplexer_3_out), .sel(control_1_out_9));
  Register #(.width(32)) PC (
    .D(multiplexer_3_out), .Q({PC_q[31:22], PC_q_2, PC_q[1:0]}), .clk(clock_1_out), .clr(in_1));  // open: en
  Clock clock_1 (.out(clock_1_out));
  Adder #(.width(32)) adder_1 (.a(32'h4), .b({PC_q[31:22], PC_q_2, PC_q[1:0]}), .out(adder_1_out));  // open: cin, cout
  ROM #(.addrWidth(20), .dataWidth(32)) rom_1 (.addr(PC_q_2), .data(rom_1_data));  // open: sel
  and and_1 (and_1_out, alu_1_branch, control_1_out_5);
  control control_1 (
    .in_1(rom_1_data[6:0]), .out_2(control_1_out_2), .out_3(control_1_out_3), .out_4(control_1_out_4),
    .out_5(control_1_out_5), .out_6(control_1_out_6), .out_7(control_1_out_7), .out_8(or_1_out[1]),
    .out_9(control_1_out_9), .out_10(control_1_out_10));
  ALU_OP alu_op_1 (.in_1(rom_1_data[14:12]), .in_2(rom_1_data[30]), .out_4(alu_op_1_out_4), .in_3(control_1_out_5));
  or or_1 (or_1_out[0], control_1_out_3, control_1_out_6, control_1_out_7, control_1_out_9);
  Multiplexer #(.width(5), .enable("false")) multiplexer_4 (
    .in0(rom_1_data[11:7]), .in1(5'b00001), .out(multiplexer_4_out), .sel(control_1_out_10));
  Multiplexer #(.width(32), .enable("false")) multiplexer_5 (
    .in0(multiplexer_10_out), .in1(adder_1_out), .out(multiplexer_5_out), .sel(control_1_out_10));
  BitExtender bitextender_1 (
    .in_1(rom_1_data), .out_3(bitextender_1_out_3), .U_TYPE(bitextender_1_u_type),
    .S_TYPE(bitextender_1_s_type), .out_6(bitextender_1_out_6), .UJ_TYPE(bitextender_1_uj_type),
    .in_2({PC_q[31:22], PC_q_2, PC_q[1:0]}));
  reg_file reg_file_1 (
    .in_1(multiplexer_5_out), .Wen(control_1_out_2), .out_8(reg_file_1_out_8), .RS1(rom_1_data[19:15]),
    .RD(multiplexer_4_out), .out_9(reg_file_1_out_9), .RS2(rom_1_data[24:20]), .in_6(clock_1_out), .in_7(in_1));
  Multiplexer #(.width(32), .enable("false")) multiplexer_6 (
    .in0(bitextender_1_out_3), .in1(bitextender_1_s_type), .out(multiplexer_6_out), .sel(control_1_out_7));
  // Probe on bitextender_1_out_6
  Multiplexer #(.width(32), .enable("false")) multiplexer_7 (
    .in0(reg_file_1_out_8), .in1(adder_1_out), .out(multiplexer_7_out), .sel(or_1_out[1]));
  Multiplexer #(.select(2), .width(32), .enable("false")) multiplexer_8 (
    .in0(reg_file_1_out_9), .in1(multiplexer_6_out), .in2(bitextender_1_u_type), .out(multiplexer_8_out),
    .sel(or_1_out));  // open: in3
  // Probe on multiplexer_6_out
  // Probe on or_1_out
  // Probe on alu_op_1_out_4
  // Probe on multiplexer_7_out
  // Probe on multiplexer_8_out
  or or_2 (or_2_out, control_1_out_7, or_1_out[1], control_1_out_3);
  // Probe on alu_1_out_4[25:2]
  ALU alu_1 (
    .in_1(multiplexer_7_out), .in_2(multiplexer_8_out), .out_4(alu_1_out_4), .in_3(multiplexer_9_out),
    .Branch(alu_1_branch));
  Multiplexer #(.width(5), .enable("false")) multiplexer_9 (
    .in0(alu_op_1_out_4), .in1({5{1'b0}}), .out(multiplexer_9_out), .sel(or_2_out));
  // Probe on reg_file_1_out_9
  // Probe on multiplexer_10_out
  RAM #(.addrWidth(24), .dataWidth(32), .bus("separate")) ram_1 (
    .addr(alu_1_out_4[25:2]), .din(reg_file_1_out_9), .data(ram_1_data), .str(control_1_out_7),
    .clk(clock_1_out), .ld(control_1_out_3));  // open: sel, clr
  Multiplexer #(.width(32), .enable("false")) multiplexer_10 (
    .in0(multiplexer_11_out), .in1(bitextender_1_u_type), .out(multiplexer_10_out), .sel(control_1_out_4));
  Multiplexer #(.width(32)) multiplexer_11 (
    .in0(alu_1_out_4), .in1(ram_1_data), .out(multiplexer_11_out), .sel(control_1_out_3));  // open: en

  // Notes on the sheet:
  //   contents of rom_1 (hex, n*v repeats v):
  //   1100f13 1e02023 693 613 593 100593 2783 60533 168693 b50633 fed780e3 16f713 fe0706e3 605b3 fe9ff0ef
endmodule

module ALU_OP (
  input  [2:0] in_1,
  input  in_2,
  input  in_3,
  output [4:0] out_4
);

  Multiplexer #(.width(5), .enable("false")) multiplexer_1 (
    .in0({1'b0, in_2, in_1}), .in1({2'b10, in_1}), .out(out_4), .sel(in_3));
endmodule

module ALU (
  input  [31:0] in_1,
  input  [31:0] in_2,
  input  [4:0] in_3,
  output [31:0] out_4,
  output Branch
);

  wire comparator_1_lt, comparator_2_lt, comparator_3_eq, comparator_4_eq, comparator_4_gt, comparator_4_lt,
       comparator_5_eq, comparator_6_eq, or_2_out;
  wire [31:0] adder_1_out, and_1_out, multiplexer_1_out, multiplexer_2_out, multiplexer_3_out,
       multiplexer_4_out, multiplexer_5_out, multiplexer_6_out, or_1_out, shifter_1_out, shifter_2_out,
       shifter_3_out, subtractor_1_out, xor_1_out;

  assign and_1_out = in_1 & in_2;  // AND_Gate and_1, 32 bits wide
  assign or_1_out = in_1 | in_2;  // OR_Gate or_1, 32 bits wide
  Adder #(.width(32)) adder_1 (.a(in_1), .b(in_2), .out(adder_1_out));  // open: cin, cout
  Comparator #(.width(32), .mode("unsigned")) comparator_1 (.a(in_1), .b(in_2), .lt(comparator_1_lt));  // open: gt, eq
  Subtractor #(.width(32)) subtractor_1 (.a(in_1), .b(in_2), .out(subtractor_1_out));  // open: bin, bout
  Shifter #(.width(32), .shift("lr")) shifter_1 (.in(in_1), .\dist (in_2[4:0]), .out(shifter_1_out));
  Shifter #(.width(32), .shift("ar")) shifter_2 (.in(in_1), .\dist (in_2[4:0]), .out(shifter_2_out));
  Shifter #(.width(32)) shifter_3 (.in(in_1), .\dist (in_2[4:0]), .out(shifter_3_out));
  assign xor_1_out = in_1 ^ in_2;  // XOR_Gate xor_1, 32 bits wide
  Comparator #(.width(32)) comparator_2 (.a(in_1), .b(in_2), .lt(comparator_2_lt));  // open: gt, eq
  Comparator #(.width(32)) comparator_3 (.a(in_1), .b(in_2), .eq(comparator_3_eq));  // open: gt, lt
  Comparator #(.width(32)) comparator_4 (
    .a(in_1), .b(in_2), .gt(comparator_4_gt), .eq(comparator_4_eq), .lt(comparator_4_lt));
  or or_2 (or_2_out, comparator_4_gt, comparator_4_eq);
  Multiplexer #(.width(32)) multiplexer_1 (
    .in0({32{1'b0}}), .in1(32'h1), .out(multiplexer_1_out), .sel(comparator_1_lt));  // open: en
  Multiplexer #(.width(32)) multiplexer_2 (
    .in0({32{1'b0}}), .in1(32'h1), .out(multiplexer_2_out), .sel(comparator_2_lt));  // open: en
  Multiplexer #(.width(32)) multiplexer_3 (
    .in0({32{1'b0}}), .in1(32'h1), .out(multiplexer_3_out), .sel(comparator_3_eq));  // open: en
  Multiplexer #(.width(32)) multiplexer_4 (
    .in0({32{1'b0}}), .in1(32'h1), .out(multiplexer_4_out), .sel(or_2_out));  // open: en
  Multiplexer #(.width(32)) multiplexer_5 (
    .in0({32{1'b0}}), .in1(32'h1), .out(multiplexer_5_out), .sel(comparator_4_eq));  // open: en
  Multiplexer #(.width(32)) multiplexer_6 (
    .in0({32{1'b0}}), .in1(32'h1), .out(multiplexer_6_out), .sel(comparator_4_lt));  // open: en
  Multiplexer #(.select(5), .width(32)) multiplexer_7 (
    .in0(adder_1_out), .in1(shifter_3_out), .in2(multiplexer_2_out), .in3(multiplexer_1_out),
    .in4(xor_1_out), .in5(shifter_1_out), .in6(or_1_out), .in7(and_1_out), .in8(subtractor_1_out),
    .in13(shifter_2_out), .in16(multiplexer_3_out), .in17(multiplexer_6_out), .in20(multiplexer_5_out),
    .in21(multiplexer_4_out), .out(out_4), .sel(in_3));  // open: in9, in10, in11, in12, in14, in15, in18, in19, in22, in23, in24, in25, in26, in27, in28, in29, in30, in31, en
  Comparator #(.width(2)) comparator_5 (.a(in_3[4:3]), .b(2'b10), .eq(comparator_5_eq));  // open: gt, lt
  Comparator #(.width(32)) comparator_6 (.a(out_4), .b(32'h1), .eq(comparator_6_eq));  // open: gt, lt
  and and_2 (Branch, comparator_5_eq, comparator_6_eq);
endmodule

module BitExtender (
  input  [31:0] in_1,
  input  [31:0] in_2,
  output [31:0] out_3,
  output [31:0] U_TYPE,
  output [31:0] S_TYPE,
  output [31:0] out_6,
  output [31:0] UJ_TYPE
);

  wire [31:0] bit_extender_2_out, bit_extender_4_out, bit_extender_5_out;

  assign out_3 = {{20{in_1[31]}}, in_1[31:20]};  // Bit_Extender bit_extender_1
  assign bit_extender_2_out = {{12{in_1[31]}}, in_1[31:12]};  // Bit_Extender bit_extender_2
  assign S_TYPE = {{20{in_1[31]}}, {in_1[31:25], in_1[11:7]}};  // Bit_Extender bit_extender_3
  // Probe on {in_1[31], in_1[7], in_1[30:25], in_1[11:8], 1'b0}
  assign bit_extender_4_out = {{19{in_1[31]}}, {in_1[31], in_1[7], in_1[30:25], in_1[11:8], 1'b0}};  // Bit_Extender bit_extender_4
  assign bit_extender_5_out = {{11{in_1[31]}}, {in_1[31], in_1[19:12], in_1[20], in_1[30:21], 1'b0}};  // Bit_Extender bit_extender_5
  Shifter #(.width(32)) shifter_1 (.in(bit_extender_2_out), .\dist (5'b01100), .out(U_TYPE));
  Adder #(.width(32)) adder_1 (.a(bit_extender_4_out), .b(in_2), .out(out_6));  // open: cin, cout
  Adder #(.width(32)) adder_2 (.a(bit_extender_5_out), .b(in_2), .out(UJ_TYPE));  // open: cin, cout

  // Notes on the sheet:
  //   I - TYPE
  //   SB-TYPE
endmodule

module control_decode (
  input  jalr,
  input  jal,
  input  Auipc,
  input  L,
  input  I,
  input  S,
  input  B,
  input  R,
  input  lui,
  output I_2,
  output S_2,
  output write_enable,
  output Load,
  output Store,
  output Branch,
  output auipc_2,
  output jalr_2,
  output jal_2
);

  wire or_1_out;

  or or_1 (or_1_out, L, I, S);
  or or_2 (write_enable, I, Auipc, L, R, lui, jal);

  assign auipc_2 = Auipc;
  assign Branch = B;
  assign I_2 = I;
  assign jal_2 = jal;
  assign jalr_2 = jalr;
  assign Load = L;
  assign S_2 = S;
  assign Store = lui;
endmodule

module opcode_ide (
  input  [6:0] in_1,
  output Load,
  output I_type,
  output S_type,
  output SB_type,
  output R_type,
  output Jalr,
  output Jal,
  output Lui,
  output auipc
);

  Comparator #(.width(7)) comparator_1 (.a(in_1), .b(7'b0000011), .eq(Load));  // open: gt, lt
  Comparator #(.width(7)) comparator_2 (.a(in_1), .b(7'b0010011), .eq(I_type));  // open: gt, lt
  Comparator #(.width(7)) comparator_3 (.a(in_1), .b(7'b0100011), .eq(S_type));  // open: gt, lt
  Comparator #(.width(7)) comparator_4 (.a(in_1), .b(7'b1100011), .eq(SB_type));  // open: gt, lt
  Comparator #(.width(7)) comparator_5 (.a(in_1), .b(7'b0110011), .eq(R_type));  // open: gt, lt
  Comparator #(.width(7)) comparator_6 (.a(in_1), .b(7'b1100111), .eq(Jalr));  // open: gt, lt
  Comparator #(.width(7)) comparator_7 (.a(in_1), .b(7'b1101111), .eq(Jal));  // open: gt, lt
  Comparator #(.width(7), .mode("unsigned")) comparator_8 (.a(in_1), .b(7'b0110111), .eq(Lui));  // open: gt, lt
  Comparator #(.width(7)) comparator_9 (.a(7'b0010111), .b(in_1), .eq(auipc));  // open: gt, lt
endmodule

module control (
  input  [6:0] in_1,
  output out_2,
  output out_3,
  output out_4,
  output out_5,
  output out_6,
  output out_7,
  output out_8,
  output out_9,
  output out_10
);

  wire opcode_ide_1_auipc, opcode_ide_1_i_type, opcode_ide_1_jal, opcode_ide_1_jalr, opcode_ide_1_load,
       opcode_ide_1_lui, opcode_ide_1_r_type, opcode_ide_1_s_type, opcode_ide_1_sb_type;

  opcode_ide opcode_ide_1 (
    .in_1(in_1), .Load(opcode_ide_1_load), .I_type(opcode_ide_1_i_type), .S_type(opcode_ide_1_s_type),
    .SB_type(opcode_ide_1_sb_type), .R_type(opcode_ide_1_r_type), .Jalr(opcode_ide_1_jalr),
    .Jal(opcode_ide_1_jal), .Lui(opcode_ide_1_lui), .auipc(opcode_ide_1_auipc));
  control_decode control_decode_1 (
    .I_2(out_6), .S_2(out_7), .Load(out_3), .Branch(out_5), .L(opcode_ide_1_load), .I(opcode_ide_1_i_type),
    .S(opcode_ide_1_s_type), .B(opcode_ide_1_sb_type), .R(opcode_ide_1_r_type), .Store(out_4),
    .lui(opcode_ide_1_lui), .Auipc(opcode_ide_1_auipc), .auipc_2(out_8), .jal(opcode_ide_1_jal),
    .jalr(opcode_ide_1_jalr), .jalr_2(out_9), .jal_2(out_10), .write_enable(out_2));
endmodule
